# Fritzing sketch node-v1 (saved by Fritzing 0.9.3b)

parts:
  Part1 = Adafruit Feather M0 RFM69 [part_number="Adafruit #3176 or #3177"]
  S1 = SWITCH-MOMENTARY-2 [package=tactile_switch_smd-2]
  Part2 = Adafruit I2S Mic - SPH0645 [part_number="Adafruit #3421"]
  LED1 = RGB LED (com. cathode, rgb) [package="5 mm [THT]"]
  R1 = Resistor [tolerance=±5% resistance=270 package=THT]
  R2 = Resistor [tolerance=±5% resistance=220 package=THT]
  R3 = Resistor [tolerance=±5% resistance=270 package=THT]
  R4 = Resistor [tolerance=±5% resistance=270 package=THT]

nets:
  N1: Part1.D1, Part2.BCLK
  N2: Part1.D0, Part2.WS
  N3: Part1.A3, S1.2, R2.Pin_1
  GND: Part1.GND, Part2.GND
  +3V3: Part1.+3V3, S1.1, Part2.VDD
  N4: Part1.D12, Part2.DATA
  N5: Part1.D11, R1.Pin_1
  N6: Part1.D10, R3.Pin_1
  N7: Part1.D5, R4.Pin_1
  N8: LED1.red_anode, R4.Pin_0
  N9: LED1.common_cathode, R3.Pin_0
  N10: LED1.green_anode, R2.Pin_0
  N11: LED1.blue_anode, R1.Pin_0

notes:
  270Ω resistor per color. Don't be tempted to only put one on the common - the brightness will vary depending on the color!
  10kΩ
  Antenna
  433Mhz = 16.4cm

custom parts:
  Adafruit Feather M0 RFM69: This is the Adafruit Feather M0 RFM69 Packet Radio - our take on an microcontroller with a RFM69HCW packet radio transceiver plus built in USB and battery charging. Its an Adafruit Feather M0 with a 433MHz or 900MHz radio module cooked in! We have other boards in the Feather family, check'em out here. At the Feather M0's heart is an ATSAMD21G18 ARM Cortex M0 processor, clocked at 48 MHz and at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
  Adafruit I2S Mic - SPH0645: For many microcontrollers, adding audio input is easy with one of our analog microphone breakouts. But as you get to bigger and better microcontrollers and microcomputers, you'll find that you don't always have an analog input, or maybe you want to avoid the noise that can seep in with an analog mic system. Once you get past 8-bit micros, you will often find an I2S peripheral, that can take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
